# Fritzing sketch distance_monitor (arduino_rpi) (saved by Fritzing 0.9.6b)
breadboards: 1

parts:
  HC-SR04_Sensor_1 = HC-SR04 Ultrasonic Distance Sensor
  HC-SR04_Sensor_2 = HC-SR04 Ultrasonic Distance Sensor
  HC-SR04_Sensor_3 = HC-SR04 Ultrasonic Distance Sensor
  HC-SR04_Sensor_4 = HC-SR04 Ultrasonic Distance Sensor
  Part1 = Arduino Mega 2560 (Rev3)

nets:
  VCC: HC-SR04_Sensor_1.VCC, HC-SR04_Sensor_2.VCC, HC-SR04_Sensor_3.VCC, HC-SR04_Sensor_4.VCC, Part1.5V
  N1: HC-SR04_Sensor_1.TRIG, Part1.D4_PWM
  N2: HC-SR04_Sensor_1.ECHO, Part1.D10_PWM
  GND: HC-SR04_Sensor_1.GND, HC-SR04_Sensor_2.GND, HC-SR04_Sensor_3.GND, HC-SR04_Sensor_4.GND, Part1.GND
  N3: HC-SR04_Sensor_2.TRIG, Part1.D5_PWM
  N4: HC-SR04_Sensor_2.ECHO, Part1.D11_PWM
  N5: HC-SR04_Sensor_3.TRIG, Part1.D3_PWM
  N6: HC-SR04_Sensor_3.ECHO, Part1.D9_PWM
  N7: HC-SR04_Sensor_4.TRIG, Part1.D2_PWM
  N8: HC-SR04_Sensor_4.ECHO, Part1.D8_PWM
