# Fritzing sketch distance_monitor (rpi_gpio) (saved by Fritzing 0.9.6b)
breadboards: 1

parts:
  Raspberry_Pi_1 = Raspberry Pi 3 [part_number=RPI-3-V1.2]
  HC-SR04_Sensor_1 = HC-SR04 Ultrasonic Distance Sensor
  R1 = Resistor [tolerance=±5% power=0.25 resistance=220 package=THT]
  R2 = Resistor [tolerance=±5% power=0.25W resistance=100 package=THT]
  HC-SR04_Sensor_2 = HC-SR04 Ultrasonic Distance Sensor
  R3 = Resistor [tolerance=±5% power=0.25 resistance=100 package=THT]
  R4 = Resistor [tolerance=±5% power=0.25 resistance=220 package=THT]

nets:
  N1: Raspberry_Pi_1.GPIO21, HC-SR04_Sensor_1.TRIG
  N2: Raspberry_Pi_1.GPIO20, R1.Pin_0, R2.Pin_0
  GND: Raspberry_Pi_1.GND, HC-SR04_Sensor_1.GND, R1.Pin_1, HC-SR04_Sensor_2.GND, R3.Pin_1, R4.Pin_0, R4.Pin_1
  N3: Raspberry_Pi_1.GPIO12, HC-SR04_Sensor_2.ECHO, R3.Pin_0
  VCC: Raspberry_Pi_1.5V, HC-SR04_Sensor_1.VCC, HC-SR04_Sensor_2.VCC
  N4: HC-SR04_Sensor_1.ECHO, R2.Pin_1

notes:
  Output from echo pin of HC-SR04 needs to be reduced from 5v to 3.3v. Diagram uses 100 + 220 ohm resistors for this.
